// Logisim project hhh.circ as structural Verilog: 1 circuit, main circuit main
module main (
  output a,
  output b,
  output c,
  output d,
  output e,
  output f,
  output g
);

  wire and_1_out, and_2_out, and_3_out, and_4_out, and_5_out, and_6_out, and_7_out, and_8_out, and_9_out,
       and_10_out, and_11_out, and_12_out, and_13_out, and_14_out, and_15_out, and_16_out, and_17_out,
       and_18_out, and_19_out, and_20_out, and_21_out, and_22_out, and_23_out, and_24_out, and_25_out,
       and_26_out, clock_1_out, d_ff_1_q, d_ff_1_qn, d_ff_2_q, d_ff_2_qn, d_ff_3_q, d_ff_3_qn, d_ff_4_q,
       d_ff_4_qn, d_ff_5_q, d_ff_5_qn, not_1_out, not_2_out, not_3_out, not_4_out, not_5_out, not_6_out,
       not_7_out, not_8_out, not_9_out, not_10_out, not_11_out, not_12_out, not_13_out, not_14_out,
       not_15_out, not_16_out, not_17_out, not_18_out, not_19_out, not_20_out, not_21_out, or_1_out,
       or_2_out, or_3_out;

  Clock clock_1 (.out(clock_1_out));
  D_Flip_Flop d_ff_1 (.clk(clock_1_out), .D(d_ff_5_qn), .Q(d_ff_1_q), .Qn(d_ff_1_qn));  // open: preset, en, reset
  D_Flip_Flop d_ff_2 (.clk(clock_1_out), .D(d_ff_1_q), .Q(d_ff_2_q), .Qn(d_ff_2_qn));  // open: preset, en, reset
  D_Flip_Flop d_ff_3 (.clk(clock_1_out), .D(d_ff_2_q), .Q(d_ff_3_q), .Qn(d_ff_3_qn));  // open: preset, en, reset
  D_Flip_Flop d_ff_4 (.clk(clock_1_out), .D(d_ff_3_q), .Q(d_ff_4_q), .Qn(d_ff_4_qn));  // open: preset, en, reset
  D_Flip_Flop d_ff_5 (.clk(clock_1_out), .D(d_ff_4_q), .Q(d_ff_5_q), .Qn(d_ff_5_qn));  // open: preset, en, reset
  and and_1 (and_1_out, d_ff_1_qn, d_ff_2_qn, d_ff_3_qn, d_ff_5_q);
  and and_2 (and_2_out, d_ff_1_q, d_ff_2_q, d_ff_3_q, d_ff_4_qn);
  and and_3 (and_3_out, d_ff_1_qn, d_ff_3_q, d_ff_4_q, d_ff_5_q);
  and and_4 (and_4_out, d_ff_1_qn, d_ff_3_q, d_ff_4_q, d_ff_5_q);
  and and_5 (and_5_out, d_ff_1_q, d_ff_2_q, d_ff_3_qn, d_ff_5_qn);
  and and_6 (and_6_out, d_ff_1_q, d_ff_2_qn, d_ff_3_qn, d_ff_4_qn, d_ff_5_qn);
  and and_7 (and_7_out, d_ff_5_qn, d_ff_4_qn, d_ff_3_q, d_ff_2_q, d_ff_1_q);
  and and_8 (and_8_out, d_ff_4_q, d_ff_5_q, d_ff_3_q, d_ff_2_q, d_ff_1_q);
  and and_9 (and_9_out, d_ff_1_qn, d_ff_2_qn, d_ff_3_q, d_ff_4_q, d_ff_5_q);
  and and_10 (and_10_out, d_ff_1_qn, d_ff_2_qn, d_ff_3_qn, d_ff_4_qn, d_ff_5_q);
  or or_1 (or_1_out, and_2_out, and_3_out);
  or or_2 (or_2_out, and_4_out, and_5_out);
  or or_3 (or_3_out, and_6_out, and_7_out, and_8_out, and_9_out, and_10_out);
  not not_1 (not_1_out, or_1_out);
  not not_2 (not_2_out, or_3_out);
  not not_3 (not_3_out, or_2_out);
  not not_4 (not_4_out, or_3_out);
  not not_5 (not_5_out, or_2_out);
  not not_6 (not_6_out, or_1_out);
  not not_7 (not_7_out, or_3_out);
  not not_8 (not_8_out, or_1_out);
  not not_9 (not_9_out, or_3_out);
  not not_10 (not_10_out, or_2_out);
  not not_11 (not_11_out, or_1_out);
  not not_12 (not_12_out, or_3_out);
  not not_13 (not_13_out, or_3_out);
  not not_14 (not_14_out, or_2_out);
  not not_15 (not_15_out, or_3_out);
  not not_16 (not_16_out, or_2_out);
  not not_17 (not_17_out, or_3_out);
  not not_18 (not_18_out, or_1_out);
  not not_19 (not_19_out, or_2_out);
  not not_20 (not_20_out, or_3_out);
  and and_11 (and_11_out, not_1_out, not_2_out);
  and and_12 (and_12_out, or_1_out, or_3_out);
  not not_21 (not_21_out, or_1_out);
  and and_13 (and_13_out, not_3_out, not_4_out);
  and and_14 (and_14_out, or_2_out, or_3_out);
  or or_4 (c, not_5_out, or_3_out, or_1_out);
  and and_15 (and_15_out, not_6_out, not_7_out);
  and and_16 (and_16_out, not_8_out, or_2_out);
  and and_17 (and_17_out, or_2_out, not_9_out);
  and and_18 (and_18_out, or_1_out, not_10_out, or_3_out);
  and and_19 (and_19_out, not_11_out, not_12_out);
  and and_20 (and_20_out, or_2_out, not_13_out);
  and and_21 (and_21_out, not_14_out, not_15_out);
  and and_22 (and_22_out, or_1_out, not_16_out);
  and and_23 (and_23_out, or_1_out, not_17_out);
  and and_24 (and_24_out, not_18_out, or_2_out);
  and and_25 (and_25_out, or_1_out, not_19_out);
  and and_26 (and_26_out, or_1_out, not_20_out);
  or or_5 (a, and_11_out, or_2_out, and_12_out, and_1_out);
  or or_6 (b, not_21_out, and_13_out, and_14_out);
  or or_7 (d, and_15_out, and_16_out, and_17_out, and_18_out, and_1_out);
  or or_8 (e, and_19_out, and_20_out);
  or or_9 (f, and_21_out, and_22_out, and_23_out, and_1_out);
  or or_10 (g, and_24_out, and_25_out, and_26_out, and_1_out);
  _7_Segment_Display u_7_segment_display_1 (.g(g), .f(f), .a(a), .b(b), .e(e), .d(d), .c(c));  // open: dp
endmodule
